# Fritzing sketch temperatureLogger (saved by Fritzing 0.9.2b)
breadboards: 1

parts:
  U1 = atmega328 [package=dip]
  C1 = Ceramic Capacitor [capacitance=100nF package="100 mil [THT, multilayer]"]
  C2 = Ceramic Capacitor [capacitance=100nF package="100 mil [THT, multilayer]"]
  XTAL1 = CRYSTAL - kHz [frequency="32 kHz"]
  VCC1 = Battery
  R1 = Resistor [tolerance=±5% resistance=220 package=THT]
  JP1 = Header 6 [package=molex-1x6_lock]
  LED3 = LED - 5mm [color="Red (633nm)" package="5 mm [THT]"]
  R2 = Resistor [tolerance=±5% resistance=47k package=THT]
  R3 = Temperature Sensor (Thermistor) [thermistor_type=NTC package=THT]
  R4 = Resistor [tolerance=±5% resistance=10k package=THT]

nets:
  N1: U1.RESET, R4.Pin_1
  N2: U1.D0_(RX), JP1.3
  N3: U1.D1_(TX), JP1.4
  N4: U1.VCC, U1.AVCC, VCC1.+, R4.Pin_0
  N5: U1.GND, C1.0, C2.0, VCC1.-, R1.Pin_1, JP1.5, R3.pin_1
  N6: U1.XLAT1, C1.1, XTAL1.pin_0
  N7: U1.XLAT2, C2.1, XTAL1.pin_1
  N8: U1.D12, R2.Pin_0
  N9: U1.D13, LED3.cathode
  N10: U1.A5, R2.Pin_1, R3.pin_0
  N11: R1.Pin_0, LED3.anode
